// Logisim project ex6_a.circ as structural Verilog: 1 circuit, main circuit main
module main (
);

  wire and_1_out, and_2_out, and_3_out, not_1_out, not_2_out, or_1_out, or_2_out, undriven, undriven_2,
       undriven_3, undriven_4;

  not not_1 (not_1_out, undriven_2);
  not not_2 (not_2_out, undriven_4);
  buf and_1 (and_1_out, not_1_out);  // AND_Gate
  and and_2 (and_2_out, undriven, not_2_out);
  or or_1 (or_1_out, and_2_out, undriven_4);
  and and_3 (and_3_out, or_1_out, undriven_3);
  or or_2 (or_2_out, and_1_out, and_3_out);

  // Notes on the sheet:
  //   A
  //   B
  //   C
  //   D
  //   b
  //   x
  //   y
  //   z
  //   w
  //   F
endmodule
