// Logisim project ex6_b.circ as structural Verilog: 1 circuit, main circuit main
module main (
);

  wire and_1_out, and_2_out, nor_1_out, nor_2_out, not_1_out, not_2_out, or_1_out, or_2_out, or_3_out,
       undriven, undriven_2, undriven_3, undriven_4, xor_1_out;

  not not_1 (not_1_out, undriven);
  not not_2 (not_2_out, undriven_2);
  xor xor_1 (xor_1_out, undriven, undriven_4);
  and and_1 (and_1_out, not_1_out, not_2_out, undriven_4);
  nor nor_1 (nor_1_out, undriven, undriven_3);
  and and_2 (and_2_out, not_2_out, undriven_3);
  or or_1 (or_1_out, not_1_out, undriven_4, undriven_3);
  or or_2 (or_2_out, xor_1_out, nor_1_out);
  nor nor_2 (nor_2_out, and_1_out, or_1_out, and_2_out);
  or or_3 (or_3_out, or_2_out, nor_2_out);

  // Notes on the sheet:
  //   X
  //   Y
  //   W
  //   Z
  //   w7
  //   w6
  //   w5
  //   w2
  //   w4
  //   w3
  //   w1
  //   F3
  //   F1
  //   F2
endmodule
