// Logisim project ex6_c.circ as structural Verilog: 1 circuit, main circuit main
module main (
);

  wire and_1_out, and_2_out, or_1_out, undriven, undriven_2;

  and and_1 (and_1_out, undriven_2, undriven);
  and and_2 (and_2_out, undriven_2, undriven);
  or or_1 (or_1_out, undriven_2, undriven);

  // Notes on the sheet:
  //   A
  //   B
  //   x1
  //   x2
  //   x3
endmodule
